# Fritzing sketch pi-pico-console (saved by Fritzing 0.9.6b)
breadboards: 1

parts:
  A1 = Raspberry Pi Pico H
  S1 = Momentary Switch [package=tactile-pth]
  FTDI_USB_UART1 = CP2102 USB UART [part_number="USB UART"]

nets:
  N1: A1.GP0, FTDI_USB_UART1.RXI
  N2: A1.GP1, FTDI_USB_UART1.TXO
  GND: A1.GND, S1.2, FTDI_USB_UART1.GND
  N3: A1.RUN, S1.3

custom parts:
  Raspberry Pi Pico H: Raspberry Pi Pico H. Based around the RP2040 microcontroller the Pico H is a low cost microcontroller device bringing Raspberry Pi quality, cost, and easy of use to the microcontroller space.
  CP2102 USB UART: CP2102 USB UART FTDI
